# Fritzing sketch loud_loud_boy_device (saved by Fritzing 0.9.3b)

parts:
  U1 = ESP8266 NodeMCU LoLin module
  S1 = Pushbutton [package="[SMD]"]
  S2 = Pushbutton [package="[SMD]"]
  J1 = Piezo Speaker
  S3 = Pushbutton [package="[SMD]"]
  OLED_I2C1 = OLED 128x64 I2C Monochrome Display
  R1 = Resistor [tolerance=±5% resistance=100k package="1206 [SMD]"]
  VCC1 = Battery

nets:
  N1: U1.D1, OLED_I2C1.SCK
  N2: U1.D2, OLED_I2C1.SDA
  3V3: U1.3V3, S1.Pin_3, S1.Pin_4, S2.Pin_3, S2.Pin_4, S3.Pin_3, S3.Pin_4, OLED_I2C1.VDD
  GND: U1.GND, J1.pin1, OLED_I2C1.GND, R1.Pin_0, VCC1.-
  N3: U1.D5, U1.D6, U1.D8, S1.Pin_1, S1.Pin_2, S2.Pin_1, S2.Pin_2, S3.Pin_1, S3.Pin_2, R1.Pin_1
  N4: U1.D7, J1.pin2
  N5: U1.Vin, VCC1.+

custom parts:
  ESP8266 NodeMCU LoLin module: ESP8266 based NodeMCU
